// Logisim project Logisim-hw01.circ as structural Verilog: 1 circuit, main circuit main
module main (
  input  A,
  input  B,
  input  A_2,
  input  B_2,
  input  C,
  input  A_3,
  input  B_3,
  input  C_2,
  input  A_4,
  input  B_4,
  input  C_3,
  input  D,
  output F,
  output F_2,
  output F_prime,
  output F_3
);

  wire and_1_out, and_2_out, and_3_out, and_4_out, not_1_out, not_2_out, not_3_out, not_4_out, not_5_out,
       not_6_out, not_7_out, not_8_out, not_9_out, or_2_out, or_3_out;

  not not_1 (not_1_out, D);
  not not_2 (not_2_out, A);
  not not_3 (not_3_out, B);
  not not_4 (not_4_out, A_2);
  not not_5 (not_5_out, B_2);
  not not_6 (not_6_out, C);
  not not_7 (not_7_out, A_3);
  not not_8 (not_8_out, B_3);
  not not_9 (not_9_out, C_2);
  or or_1 (F_3, A_4, not_1_out);
  and and_1 (and_1_out, not_2_out, not_3_out);
  and and_2 (and_2_out, B, A);
  and and_3 (and_3_out, not_4_out, not_5_out, not_6_out);
  and and_4 (and_4_out, C, B_2, A_2);
  or or_2 (or_2_out, not_7_out, not_8_out, not_9_out);
  or or_3 (or_3_out, C_2, B_3, A_3);
  or or_4 (F, and_1_out, and_2_out);
  or or_5 (F_2, and_3_out, and_4_out);
  and and_5 (F_prime, or_2_out, or_3_out);

  // Notes on the sheet:
  //   第2题
  //   第3题
  //   第4题
endmodule
