// Logisim project hw04-3.circ as structural Verilog: 1 circuit, main circuit main
module main (
  input  X,
  output Z
);

  wire and_1_out, and_2_out, clock_1_out, d_ff_1_q, d_ff_2_q, d_ff_2_qn, or_1_out, or_2_out;

  Clock clock_1 (.out(clock_1_out));
  and and_1 (and_1_out, X, or_1_out);
  or or_1 (or_1_out, d_ff_2_q, d_ff_1_q);
  D_Flip_Flop d_ff_1 (.clk(clock_1_out), .D(and_1_out), .Q(d_ff_1_q));  // open: Qn, preset, en, reset
  and and_2 (and_2_out, X, or_2_out);
  or or_2 (or_2_out, d_ff_1_q, d_ff_2_qn);
  D_Flip_Flop d_ff_2 (.clk(clock_1_out), .D(and_2_out), .Q(d_ff_2_q), .Qn(d_ff_2_qn));  // open: preset, en, reset
  and and_3 (Z, d_ff_2_q, d_ff_1_q, X);

  // Notes on the sheet:
  //   D2
  //   D1
endmodule
