// Logisim project hw03.circ as structural Verilog: 1 circuit, main circuit main
module main (
  input  CLR,
  input  \_4个输入 ,
  input  in_3,
  input  in_4,
  input  in_5,
  output \_4个输出 ,
  output out_7,
  output out_8,
  output out_9
);

  wire clock_1_out;

  Clock clock_1 (.out(clock_1_out));
  D_Flip_Flop d_ff_1 (.clk(clock_1_out), .D(\_4个输入 ), .Q(\_4个输出 ), .reset(CLR));  // open: Qn, preset, en
  D_Flip_Flop d_ff_2 (.clk(clock_1_out), .D(in_3), .Q(out_7), .reset(CLR));  // open: Qn, preset, en
  D_Flip_Flop d_ff_3 (.clk(clock_1_out), .D(in_4), .Q(out_8), .reset(CLR));  // open: Qn, preset, en
  D_Flip_Flop d_ff_4 (.clk(clock_1_out), .D(in_5), .Q(out_9), .reset(CLR));  // open: Qn, preset, en

  // Notes on the sheet:
  //   第1题
  //   CLK
  //   第3题
  //   CP
  //   Q
  //   Y
  //   第6题
  //   CP
  //   A
  //   Q0
  //   Q1
  //   F
endmodule
